// Logisim project pr_7.circ as structural Verilog: 1 circuit, main circuit main
module main (
  input  B0,
  input  B1,
  input  B2,
  input  B3,
  input  M,
  input  in_6,
  input  A1,
  input  A2,
  input  A3,
  output out_10,
  output s2,
  output s3,
  output out_13,
  output s1
);

  wire adder_1_cout, adder_2_cout, adder_3_cout, xor_1_out, xor_2_out, xor_3_out, xor_4_out;

  xor xor_1 (xor_1_out, B0, M);
  Adder #(.width(1)) adder_1 (.a(xor_1_out), .b(in_6), .out(out_13), .cin(M), .cout(adder_1_cout));
  xor xor_2 (xor_2_out, B1, M);
  Adder #(.width(1)) adder_2 (.a(xor_2_out), .b(A1), .out(s1), .cin(adder_1_cout), .cout(adder_2_cout));
  xor xor_3 (xor_3_out, B2, M);
  Adder #(.width(1)) adder_3 (.a(xor_3_out), .b(A2), .out(s2), .cin(adder_2_cout), .cout(adder_3_cout));
  xor xor_4 (xor_4_out, B3, M);
  Adder #(.width(1)) adder_4 (.a(xor_4_out), .b(A3), .out(s3), .cin(adder_3_cout), .cout(out_10));

  // Notes on the sheet:
  //   A0
  //   C0
  //   s0
  //   c1
  //   c2
  //   B3
  //   c3
  //   c4
endmodule
